// Digital circuit Prototipo UWU.dig as structural Verilog
module Prototipo_UWU (
  input  X,
  input  clk,
  output S0,
  output S1,
  output S2,
  output S3
);

  wire and_1_out, and_2_out, and_3_out, and_8_out, and_9_out, d_ff_1_q, d_ff_2_q, not_1_out, not_2_out,
       not_3_out, not_4_out, not_5_out, not_6_out, not_7_out, not_8_out, not_9_out, or_1_out, or_2_out;

  not not_1 (not_1_out, X);
  not not_2 (not_2_out, d_ff_1_q);
  not not_3 (not_3_out, d_ff_2_q);
  and and_1 (and_1_out, not_1_out, d_ff_1_q);
  and and_2 (and_2_out, X, not_2_out, d_ff_2_q);
  and and_3 (and_3_out, d_ff_1_q, not_3_out);
  or or_1 (or_1_out, and_1_out, and_2_out, and_3_out);
  D_FF d_ff_1 (.D(or_1_out), .C(clk), .Q(d_ff_1_q));  // open: nQ
  not not_4 (not_4_out, d_ff_1_q);
  not not_5 (not_5_out, d_ff_2_q);
  not not_6 (not_6_out, d_ff_1_q);
  not not_7 (not_7_out, d_ff_2_q);
  and and_4 (S0, X, not_4_out, not_5_out);
  and and_5 (S1, X, not_6_out, d_ff_2_q);
  and and_6 (S2, X, d_ff_1_q, not_7_out);
  and and_7 (S3, X, d_ff_1_q, d_ff_2_q);
  not not_8 (not_8_out, X);
  not not_9 (not_9_out, d_ff_2_q);
  and and_8 (and_8_out, not_8_out, d_ff_2_q);
  and and_9 (and_9_out, X, not_9_out);
  or or_2 (or_2_out, and_8_out, and_9_out);
  D_FF d_ff_2 (.D(or_2_out), .C(clk), .Q(d_ff_2_q));  // open: nQ
endmodule
