// Digital circuit digitalBCDto7seg.dig as structural Verilog
module digitalBCDto7seg (
  input  in_1,
  input  in_2,
  input  in_3,
  input  in_4,
  input  in_5,
  input  in_6,
  input  in_7,
  input  in_8,
  input  in_9
);

  wire demultiplexer_1_out_0, demultiplexer_1_out_1, u_bcd7seg_n, u_bcd7seg_s, u_bcd7seg_t, u_bcd7seg_u,
       u_bcd7seg_v, u_bcd7seg_w, u_bcd7seg_x, u_bcd7seg_y, u_mux8a4_a, u_mux8a4_b, u_mux8a4_c, u_mux8a4_d;

  mux8a4 #(.applicationType("IVERILOG"), .CodeFile("mux8a4.v")) u_mux8a4 (
    .A0(in_5), .A1(in_4), .A2(in_3), .A3(in_2), .B0(in_9), .B1(in_8), .B2(in_7), .B3(in_6), .control(in_1),
    .A(u_mux8a4_a), .B(u_mux8a4_b), .C(u_mux8a4_c), .D(u_mux8a4_d));
  bcd7seg #(.applicationType("IVERILOG"), .CodeFile("bcd7seg.v")) u_bcd7seg (
    .A(u_mux8a4_a), .B(u_mux8a4_b), .C(u_mux8a4_c), .D(u_mux8a4_d), .Y(u_bcd7seg_y), .X(u_bcd7seg_x),
    .W(u_bcd7seg_w), .V(u_bcd7seg_v), .U(u_bcd7seg_u), .T(u_bcd7seg_t), .S(u_bcd7seg_s), .N(u_bcd7seg_n));
  Demultiplexer demultiplexer_1 (.sel(in_1), .in(1'b1), .out_0(demultiplexer_1_out_0), .out_1(demultiplexer_1_out_1));
  Seven_Seg #(.commonCathode("true"), .commonConnectionType("anode")) seven_seg_1 (
    .a(u_bcd7seg_y), .b(u_bcd7seg_x), .c(u_bcd7seg_w), .d(u_bcd7seg_v), .e(u_bcd7seg_u), .f(u_bcd7seg_t),
    .g(u_bcd7seg_s), .dp(u_bcd7seg_n), .common(demultiplexer_1_out_0));
  Seven_Seg #(.commonCathode("true"), .commonConnectionType("anode")) seven_seg_2 (
    .a(u_bcd7seg_y), .b(u_bcd7seg_x), .c(u_bcd7seg_w), .d(u_bcd7seg_v), .e(u_bcd7seg_u), .f(u_bcd7seg_t),
    .g(u_bcd7seg_s), .dp(u_bcd7seg_n), .common(demultiplexer_1_out_1));
endmodule
