// Digital circuit sieteSegmentos4.dig as structural Verilog
module sieteSegmentos4 (
  input  A,
  input  B,
  input  C,
  input  D,
  input  E,
  input  F,
  output Y,
  output X,
  output W,
  output V,
  output U,
  output T,
  output S,
  output R
);

  wire and_1_out, and_2_out, and_3_out, and_4_out, and_5_out, and_6_out, and_7_out, and_8_out, and_9_out,
       and_10_out, and_11_out, and_12_out, and_13_out, and_14_out, and_15_out, and_16_out, and_17_out,
       and_18_out, and_19_out, and_20_out, and_21_out, and_22_out, and_23_out, and_24_out, and_25_out,
       and_26_out, and_27_out, and_28_out, and_29_out, and_30_out, and_31_out, and_32_out, and_33_out,
       and_34_out, and_35_out, and_36_out, not_1_out, not_2_out, not_3_out, not_4_out, not_5_out;

  not not_1 (not_1_out, A);
  not not_2 (not_2_out, B);
  not not_3 (not_3_out, C);
  not not_4 (not_4_out, D);
  not not_5 (not_5_out, E);
  and and_1 (and_1_out, A, C);
  and and_2 (and_2_out, A, B);
  and and_3 (and_3_out, not_1_out, B, D);
  and and_4 (and_4_out, not_1_out, B, C);
  and and_5 (and_5_out, A, not_2_out, not_3_out);
  and and_6 (and_6_out, not_1_out, C, D, E);
  and and_7 (and_7_out, not_1_out, not_2_out, C, E);
  and and_8 (and_8_out, not_1_out, not_2_out, C, D);
  and and_9 (and_9_out, not_1_out, B, not_3_out, not_4_out);
  and and_10 (and_10_out, A, not_3_out, D);
  and and_11 (and_11_out, A, not_2_out, not_3_out);
  and and_12 (and_12_out, A, B, C);
  and and_13 (and_13_out, B, not_3_out, not_4_out, E);
  and and_14 (and_14_out, not_1_out, not_2_out, C, not_4_out, not_5_out);
  and and_15 (and_15_out, not_1_out, B, not_3_out, not_4_out, E);
  and and_16 (and_16_out, A, not_2_out, not_3_out, D, E);
  and and_17 (and_17_out, A, B, not_3_out, not_4_out, not_5_out);
  and and_18 (and_18_out, A, B, C, E);
  and and_19 (and_19_out, B, C, D, not_5_out);
  and and_20 (and_20_out, A, not_2_out, not_3_out, not_4_out, E);
  and and_21 (and_21_out, not_1_out, B, not_4_out, not_5_out);
  and and_22 (and_22_out, A, not_2_out, D, not_5_out);
  and and_23 (and_23_out, A, B, D, E);
  and and_24 (and_24_out, not_1_out, not_2_out, not_3_out, D);
  and and_25 (and_25_out, not_1_out, B, C, not_4_out);
  and and_26 (and_26_out, not_2_out, C, D, E);
  and and_27 (and_27_out, B, C, not_4_out, not_5_out);
  and and_28 (and_28_out, not_1_out, not_2_out, C, D, not_5_out);
  and and_29 (and_29_out, not_1_out, B, not_3_out, not_4_out, not_5_out);
  and and_30 (and_30_out, not_1_out, B, C, not_4_out, E);
  and and_31 (and_31_out, not_1_out, not_3_out, D, E);
  and and_32 (and_32_out, A, not_3_out, D, not_5_out);
  and and_33 (and_33_out, not_1_out, not_2_out, not_3_out, E);
  and and_34 (and_34_out, A, not_2_out, not_3_out, not_5_out);
  and and_35 (and_35_out, A, not_2_out, C, E);
  and and_36 (and_36_out, A, B, C, not_5_out);
  or or_1 (X, and_1_out, and_2_out);
  or or_2 (W, and_3_out, and_4_out, and_5_out);
  or or_3 (V, and_6_out, and_7_out, and_8_out, and_9_out, and_10_out, and_11_out, and_12_out, and_13_out);
  or or_4 (U, and_14_out, and_15_out, and_16_out, and_17_out, and_18_out, and_19_out);
  or or_5 (T, and_20_out, and_21_out, and_22_out, and_23_out, and_24_out, and_25_out, and_26_out, and_27_out);
  or or_6 (S, and_28_out, and_29_out, and_30_out, and_31_out, and_32_out, and_33_out, and_34_out, and_35_out, and_36_out);

  assign R = F;
  assign Y = 1'b0;
endmodule
